# Fritzing sketch GetBinary (saved by Fritzing 0.9.3b)
breadboards: 1

parts:
  J1 = Raspberry Pi Header 40pin [form="♂ (male)" package=THT]  # not connected
  D1 = LTE-302 [package=lte-302]
  D2 = LTE-302 [package=lte-302]
  D3 = LTE-302 [package=lte-302]
  D4 = LTE-302 [package=lte-302]
  D5 = LTE-302 [package=lte-302]
  D6 = LTE-302 [package=lte-302]
  D7 = LTE-302 [package=lte-302]
  D8 = LTE-302 [package=lte-302]
  R1 = Resistor [tolerance=±5% resistance=470 package=THT]
  R2 = Resistor [tolerance=±5% resistance=470 package=THT]
  R3 = Resistor [tolerance=±5% resistance=470 package=THT]
  R4 = Resistor [tolerance=±5% resistance=470 package=THT]
  R5 = Resistor [tolerance=±5% resistance=470 package=THT]
  R6 = Resistor [tolerance=±5% resistance=470 package=THT]
  R7 = Resistor [tolerance=±5% resistance=470 package=THT]
  R8 = Resistor [tolerance=±5% resistance=470 package=THT]

nets:
  N1: D1.A, R1.Pin_0
  N2: D2.A, R2.Pin_0
  N3: D3.A, R3.Pin_0
  N4: D4.A, R4.Pin_0
  N5: D5.A, R5.Pin_0
  N6: D6.A, R6.Pin_0
  N7: D7.A, R7.Pin_0
  N8: D8.A, R8.Pin_0

custom parts:
  Raspberry Pi Header 40pin: Raspberry Pi 40 pin header - for creating your own shields.
