# Fritzing sketch WeatherPi_PCB (saved by Fritzing 0.9.3b)
circuit board: 8.46667cm x 5.64444cm
breadboards: 1

parts:
  IC1 = IC, DIP package, 16 pins [chip_label=MCP3008]
  J1 = screw terminal, 4 pins  # not connected
  J2 = Screw terminal - 2 pins [package=THT]
  RHT1 = Humidity and Temperature Sensor RHT03
  R1 = Resistor [tolerance=±5% resistance=220 package=THT]
  J3 = Raspberry Pi Header 40pin [form="♂ (male)" package=THT]

nets:
  N1: IC1.pin9, RHT1.Data-signal, J3.5V
  N2: IC1.pin10, J3.GIPO25
  N3: IC1.pin11, J3.GIPO24
  N4: IC1.pin12, J3.GIPO23
  N5: IC1.pin13, J3.GIPO18
  3V3: IC1.pin15, IC1.pin16, J2.pin2, RHT1.Vcc, RHT1.GND_2, R1.Pin_1, J3.3v3, J3.3V3
  N6: J2.pin1, J3.GIPO20
  N7: RHT1.GND_1, R1.Pin_0, J3.GIPO16

notes:
  Anemometer
  Power
  Wind Dir
  Ground
  Wind Speed
  Rain
  Power
  Pluse

custom parts:
  Raspberry Pi Header 40pin: Raspberry Pi 40 pin header - for creating your own shields.
